# Fritzing sketch receiver (saved by Fritzing 0.8.3b)
breadboards: 1

parts:
  Part1 = Arduino Leonardo (Rev3b)
  U1 = RF-LINK_RX [package=rf-link_rx]

nets:
  5V: Part1.5V, U1.+5V
  GND: Part1.GND, U1.GND
  N1: Part1.D12/A11, U1.DATA
