# Fritzing sketch transmitter (saved by Fritzing 0.8.3b)
breadboards: 1

parts:
  Part1 = Arduino Leonardo (Rev3b)
  U1 = RF-LINK_TX [package=rf-link_tx]
  R1 = Photocell (LDR) [package=THT]
  R2 = Resistor [tolerance=±5% resistance=1k package=THT]
  S1 = Reed switch [package=THT]

nets:
  5V: Part1.IOREF, Part1.5V, U1.+5V, R1.pin_1
  GND: Part1.GND, U1.GND, R2.Pin_0, S1.pin_1
  N1: Part1.A0, R1.pin_0, R2.Pin_1
  N2: Part1.D8/A8, S1.pin_2
  N3: Part1.D12/A11, U1.DATA
